# Fritzing sketch wiring_map (saved by Fritzing 0.9.4)
breadboards: 1

parts:
  Part1 = Arduino Mega 2560 (Rev3)
  motor_encoder = AMT103
  pendulum_encoder = AMT103
  M1 = BTS7960
  M2 = DC Motor
  U1 = BATTERY-2 [package=battery-aa]
  BAT2 = BC9VPC [package=bc9vpc]

nets:
  N1: Part1.D21/SCL, pendulum_encoder.A
  N2: Part1.D20/SDA, U1.+1
  N3: Part1.D19/RX1, motor_encoder.B
  N4: Part1.D18/TX1, motor_encoder.A
  5V: Part1.5V, pendulum_encoder.5V, M1.pin7
  GND: Part1.GND, pendulum_encoder.GND, M1.pin8
  N5: Part1.D5_PWM, M1.pin2
  N6: Part1.D6_PWM, M1.pin1
  N7: pendulum_encoder.B, U1.-1
  N8: M1.pin9, M2.pin_2
  N9: M1.pin10, M2.pin_1
  N10: M1.pin11, BAT2.V+
  N11: M1.pin12, BAT2.V-

notes:
  24 v

custom parts:
  BTS7960: BTS7960 43A Peak Power H-Bridge PWM Motor Driver
